// Logisim project cpu.circ as structural Verilog: 5 circuits, main circuit main
module main (
);

  wire and_1_out, decoder_1_out9, decoder_1_out10, decoder_1_out12, not_1_out, not_2_out, not_3_out, reset,
       tick;
  wire [1:0] decoder_1_out1;
  wire [2:0] bit_extender_1_out;
  wire [6:0] bit_extender_2_out;
  wire [7:0] adder_1_out, alu_1_output1, DATA_RAM_dout, multiplexer_1_out, multiplexer_2_out,
       multiplexer_3_out, PC_q, ram_1_dout, registerfile_1_outreg1, registerfile_1_outreg2, undriven;
  wire [15:0] rom_1_data;

  Button button_1 (.out(reset));
  Clock clock_1 (.out(tick));
  // Probe on multiplexer_1_out
  Register PC (.D(multiplexer_1_out), .en(tick), .clk(tick), .Q(PC_q), .clr(reset));
  not not_1 (not_1_out, decoder_1_out9);
  Multiplexer #(.enable("false"), .width(8)) multiplexer_1 (
    .in0(registerfile_1_outreg2), .in1(adder_1_out), .out(multiplexer_1_out), .sel(not_1_out));
  Adder adder_1 (.a(8'h1), .b(PC_q), .out(adder_1_out));  // open: cin, cout
  ROM #(.dataWidth(16)) rom_1 (.addr(PC_q), .data(rom_1_data));
  // Probe on adder_1_out
  // Probe on rom_1_data
  Decoder #(.enable("false"), .select(4)) decoder_1 (
    .out1(decoder_1_out1[0]), .out9(decoder_1_out9), .out10(decoder_1_out10), .out11(decoder_1_out1[1]),
    .out12(decoder_1_out12), .sel(rom_1_data[15:12]));  // open: out0, out2, out3, out4, out5, out6, out7, out8, out13, out14, out15
  // Probe on decoder_1_out1
  and and_1 (and_1_out, rom_1_data[11], not_2_out);
  not not_2 (not_2_out, decoder_1_out12);
  Bit_Extender #(.in_width(4), .out_width(3)) bit_extender_1 (.in(rom_1_data[15:12]), .out(bit_extender_1_out));
  // Probe on multiplexer_2_out
  Multiplexer #(.enable("false"), .select(2), .width(8)) multiplexer_2 (
    .in0(alu_1_output1), .in1(rom_1_data[7:0]), .in2(DATA_RAM_dout), .out(multiplexer_2_out),
    .sel(decoder_1_out1));  // open: in3
  // Probe on rom_1_data[10:8]
  // Probe on rom_1_data[2:0]
  // Probe on registerfile_1_outreg2
  // Probe on registerfile_1_outreg2
  // Probe on decoder_1_out12
  RegisterFile registerfile_1 (
    .WriteData(multiplexer_2_out), .WriteReg(rom_1_data[10:8]), .ReadReg1(rom_1_data[10:8]),
    .WriteEnable(and_1_out), .ReadReg2(rom_1_data[2:0]), .clock(tick), .Clear(reset),
    .OutReg2(registerfile_1_outreg2), .OutReg1(registerfile_1_outreg1));
  not not_3 (not_3_out, decoder_1_out12);
  // Probe on registerfile_1_outreg1
  RAM DATA_RAM (
    .addr(registerfile_1_outreg2), .we(decoder_1_out12), .oe(not_3_out), .clk(tick),
    .din(registerfile_1_outreg1), .dout(DATA_RAM_dout));
  RAM #(.trigger("falling")) ram_1 (
    .addr(undriven), .we(decoder_1_out12), .oe(not_3_out), .clk(tick), .dout(ram_1_dout));  // open: din
  ALU alu_1 (
    .input1(registerfile_1_outreg1), .input2(registerfile_1_outreg2), .op(bit_extender_1_out),
    .output1(alu_1_output1));
  Multiplexer #(.enable("false"), .width(8)) multiplexer_3 (
    .in0({8{1'b0}}), .in1(registerfile_1_outreg2), .out(multiplexer_3_out), .sel(decoder_1_out10));
  // Probe on DATA_RAM_dout
  // Probe on ram_1_dout
  Bit_Extender #(.out_width(7)) bit_extender_2 (.in(multiplexer_3_out), .out(bit_extender_2_out));
  TTY tty_1 (.data(bit_extender_2_out), .clk(tick), .clr(reset));  // open: we

  // Notes on the sheet:
  //   contents of rom_1 (hex, n*v repeats v):
  //   1848 a008 1845 a008 184c a008 184c a008 184f a008 1802 1903 2809 1930 2809 c803 a008 1c00 bd0c bd0c
  //   bd0c a008 1c00 bd0c 1c01 cd0c 1c02 cd0c 1c03 cd0c 1800 9080
endmodule

module RegisterFile (
  input  [7:0] WriteData,
  input  [2:0] WriteReg,
  input  [2:0] ReadReg1,
  input  WriteEnable,
  input  [2:0] ReadReg2,
  input  clock,
  input  Clear,
  output [7:0] OutReg2,
  output [7:0] OutReg1
);

  wire decoder_1_out0, decoder_1_out1, decoder_1_out2, decoder_1_out3, decoder_1_out4, decoder_1_out5,
       decoder_1_out6, decoder_1_out7;
  wire [7:0] register_1_q, register_2_q, register_3_q, register_4_q, register_5_q, register_6_q,
       register_7_q, register_8_q;

  Decoder #(.select(3)) decoder_1 (
    .out0(decoder_1_out0), .out1(decoder_1_out1), .out2(decoder_1_out2), .out3(decoder_1_out3),
    .out4(decoder_1_out4), .out5(decoder_1_out5), .out6(decoder_1_out6), .out7(decoder_1_out7),
    .sel(WriteReg), .en(WriteEnable));
  Register #(.trigger("falling")) register_1 (
    .D(WriteData), .en(decoder_1_out0), .clk(clock), .Q(register_1_q), .clr(Clear));
  Register #(.trigger("falling")) register_2 (
    .D(WriteData), .en(decoder_1_out1), .clk(clock), .Q(register_2_q), .clr(Clear));
  Register #(.trigger("falling")) register_3 (
    .D(WriteData), .en(decoder_1_out2), .clk(clock), .Q(register_3_q), .clr(Clear));
  Register #(.trigger("falling")) register_4 (
    .D(WriteData), .en(decoder_1_out3), .clk(clock), .Q(register_4_q), .clr(Clear));
  Register #(.trigger("falling")) register_5 (
    .D(WriteData), .en(decoder_1_out4), .clk(clock), .Q(register_5_q), .clr(Clear));
  Register #(.trigger("falling")) register_6 (
    .D(WriteData), .en(decoder_1_out5), .clk(clock), .Q(register_6_q), .clr(Clear));
  Register #(.trigger("falling")) register_7 (
    .D(WriteData), .en(decoder_1_out6), .clk(clock), .Q(register_7_q), .clr(Clear));
  Register #(.trigger("falling")) register_8 (
    .D(WriteData), .en(decoder_1_out7), .clk(clock), .Q(register_8_q), .clr(Clear));
  Multiplexer #(.enable("false"), .select(3), .width(8)) multiplexer_1 (
    .in0(register_1_q), .in1(register_2_q), .in2(register_3_q), .in3(register_4_q), .in4(register_5_q),
    .in5(register_6_q), .in6(register_7_q), .in7(register_8_q), .out(OutReg2), .sel(ReadReg2));
  Multiplexer #(.enable("false"), .select(3), .width(8)) multiplexer_2 (
    .in0(register_1_q), .in1(register_2_q), .in2(register_3_q), .in3(register_4_q), .in4(register_5_q),
    .in5(register_6_q), .in6(register_7_q), .in7(register_8_q), .out(OutReg1), .sel(ReadReg1));
endmodule

module TestTestRegisterFiule (
  input  [7:0] in_1,
  input  [2:0] in_2,
  input  [2:0] in_3,
  input  in_4,
  input  [2:0] in_5,
  output [15:0] out_6,
  output [15:0] out_7
);

  wire clock_1_out;

  Clock clock_1 (.out(clock_1_out));
  // RegisterFile registerfile_1: pin names not known; wires that end beside it: in_1, in_2, in_3, in_4, in_5, clock_1_out, out_6, out_7
endmodule

module ALU (
  input  [7:0] input1,
  input  [7:0] input2,
  input  [2:0] op,
  output [7:0] output1
);

  wire [7:0] adder_1_out, divider_1_out, multiplier_1_out, subtractor_1_out;

  Adder adder_1 (.a(input1), .b(input2), .out(adder_1_out));  // open: cin, cout
  Subtractor subtractor_1 (.a(input1), .b(input2), .out(subtractor_1_out));  // open: bin, bout
  Multiplier multiplier_1 (.a(input1), .b(input2), .out(multiplier_1_out));  // open: cin, cout
  Divider divider_1 (.a(input1), .b(input2), .out(divider_1_out));  // open: upper, rem
  Multiplexer #(.enable("false"), .select(3), .width(8)) multiplexer_1 (
    .in2(adder_1_out), .in3(subtractor_1_out), .in4(multiplier_1_out), .in5(divider_1_out), .out(output1),
    .sel(op));  // open: in0, in1, in6, in7
endmodule

module TestMemopry (
  input  [7:0] in_1,
  input  in_2,
  input  [7:0] in_3
);

  wire clock_1_out, not_1_out;
  wire [7:0] ram_1_dout;

  Clock clock_1 (.out(clock_1_out));
  not not_1 (not_1_out, in_2);
  RAM ram_1 (.addr(in_1), .we(not_1_out), .oe(in_2), .clk(clock_1_out), .din(in_3), .dout(ram_1_dout));
  // Probe on ram_1_dout
endmodule
